# Fritzing sketch receive (saved by Fritzing 0.9.6b)

parts:
  Part3 = Adafruit Feather M0 RFM69 [part_number="Adafruit #3176 or #3177"]
  Part4 = NeoPixel Stick [part_number=1426]

nets:
  N1: Part3.A1, Part4.DATAIN
  GND: Part3.GND, Part4.GND
  +3V3: Part3.+3V3, Part4.+5V

custom parts:
  Adafruit Feather M0 RFM69: This is the Adafruit Feather M0 RFM69 Packet Radio - our take on an microcontroller with a RFM69HCW packet radio transceiver plus built in USB and battery charging. Its an Adafruit Feather M0 with a 433MHz or 900MHz radio module cooked in! We have other boards in the Feather family, check'em out here. At the Feather M0's heart is an ATSAMD21G18 ARM Cortex M0 processor, clocked at 48 MHz and at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
  NeoPixel Stick: Make your own little LED strip arrangement with this stick of NeoPixel LEDs. We crammed 8 of the tiny 5050 (5mm x 5mm) smart RGB LEDs onto a PCB with mounting holes and a chainable design. Use only one microcontroller pin to control as many as you can chain together! Each LED is addressable as the driver chip is inside the LED. Each one has ~18mA constant current drive so the color will be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
