# Fritzing sketch send (saved by Fritzing 0.9.6b)
breadboards: 1

parts:
  Part1 = Adafruit Feather M0 RFM69 [part_number="Adafruit #3176 or #3177"]
  U1 = POT [package=pot_alpha_rv16af-20]
  S1 = Pushbutton [package="[SMD]"]
  S2 = Pushbutton [package="[SMD]"]
  U2 = SWITCH_SPDT [package=kps-1290]
  S3 = Pushbutton [package="[SMD]"]
  S4 = Pushbutton [package="[SMD]"]

nets:
  N1: Part1.A1, U1.S
  N2: Part1.GND, U1.E, S1.Pin_3, S1.Pin_4, S2.Pin_3, S2.Pin_4, U2.O, S3.Pin_3, S3.Pin_4
  N3: Part1.+3V3, U1.A
  N4: Part1.D12, S1.Pin_1, S1.Pin_2
  N5: Part1.D11, S2.Pin_1, S2.Pin_2
  N6: Part1.D10, U2.S
  N7: Part1.D9, S3.Pin_1, S3.Pin_2
  N8: S4.Pin_1, S4.Pin_2
  N9: S4.Pin_3, S4.Pin_4

custom parts:
  Adafruit Feather M0 RFM69: This is the Adafruit Feather M0 RFM69 Packet Radio - our take on an microcontroller with a RFM69HCW packet radio transceiver plus built in USB and battery charging. Its an Adafruit Feather M0 with a 433MHz or 900MHz radio module cooked in! We have other boards in the Feather family, check'em out here. At the Feather M0's heart is an ATSAMD21G18 ARM Cortex M0 processor, clocked at 48 MHz and at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
